# Fritzing sketch air-monitor (saved by Fritzing 0.9.3b)
breadboards: 1

parts:
  Teensy_3_1 = Teensy 3.1
  R1 = Resistor [tolerance=±5% resistance=4.7k package=THT]
  IC1 = IC, DIP package, 6 pins [chip_label=IAQ]
  R2 = Resistor [tolerance=±5% resistance=4.7k package=THT]
  IC2 = IC, SIP package, 4 pins [chip_label=MQ135]
  IC3 = IC, DIP package, 16 pins [chip_label=HM-11]
  IC4 = IC, SIP package, 6 pins [chip_label=BME280]

nets:
  N1: Teensy_3_1.GND, IC1.pin3, IC2.pin3, IC3.pin12, IC4.pin1
  N2: Teensy_3_1.D0, IC3.pin2
  N3: Teensy_3_1.D1, IC3.pin4
  N4: Teensy_3_1.D10, IC4.pin6
  N5: Teensy_3_1.D11, IC4.pin4
  N6: Teensy_3_1.D12, IC4.pin5
  N7: Teensy_3_1.D13, IC4.pin3
  N8: Teensy_3_1.A0/D14, IC2.pin1
  N9: Teensy_3_1.A4/D18, IC1.pin4, R2.Pin_0
  N10: Teensy_3_1.A5/D19, R1.Pin_1, IC1.pin2
  N11: Teensy_3_1.3V3, R1.Pin_0, IC1.pin6, R2.Pin_1, IC3.pin9, IC4.pin2
  N12: Teensy_3_1.Vin, IC2.pin4
